# Fritzing sketch Double_Bottom_USB_Stick_Sketch (saved by Fritzing 0.9.3b)
breadboards: 1

parts:
  J1 = STM32 Nucleo boards
  CONN1 = USB connector [package=THT]
  U1 = microSD Socket [package="Molex 502774-0891 [SMD]"]  # not connected
  R1 = Resistor [tolerance=±5% resistance=220 package="2010 [SMD]"]
  R2 = Resistor [tolerance=±5% resistance=220 package="2010 [SMD]"]
  R3 = Resistor [tolerance=±5% resistance=220 package="2010 [SMD]"]
  R4 = Resistor [tolerance=±5% resistance=220 package="2010 [SMD]"]  # not connected
  R5 = Resistor [tolerance=±5% resistance=220 package="2010 [SMD]"]
  R6 = Resistor [tolerance=±5% resistance=220 package="2010 [SMD]"]
  C1 = Capacitor [package=axial-5mm]  # not connected
  C2 = Ceramic Capacitor [capacitance=100nF package="100 mil [THT, multilayer]"]
  LED1 = smd LED [color="Red (633nm)" package="0805 [SMD]"]

nets:
  N1: J1.PC8, J1.3V3, J1.PB2, J1.PB0
  N2: J1.PA12, CONN1.d+
  N3: J1.PA11, CONN1.d-
  N4: J1.PC11, J1.PD2, J1.GND#1188, J1.PB1
  N5: J1.GND#2223, CONN1.chassis5
  N6: J1.PA9, CONN1.5V
  N7: R1.Pin_0, R2.Pin_0, R3.Pin_0, LED1.anode
  N8: R1.Pin_1, R2.Pin_1, R3.Pin_1
  N9: R5.Pin_0, R6.Pin_0, C2.0
  N10: R5.Pin_1, R6.Pin_1
